// Logisim project 12bitReg.circ as structural Verilog: 1 circuit, main circuit main
module main (
  input  [11:0] INPUT,
  input  CLK,
  input  INC,
  input  LD,
  input  CLR,
  output [11:0] OUTPUT
);

  wire adder_1_cout, and_1_out, and_2_out, not_1_out, not_2_out, not_3_out;
  wire [11:0] adder_1_out, controlled_buffer_1_out, multiplexer_1_out;

  assign controlled_buffer_1_out = LD ? INPUT : 12'bz;  // Controlled_Buffer controlled_buffer_1
  Adder #(.width(12)) adder_1 (.a(OUTPUT), .b({12{1'b0}}), .out(adder_1_out), .cin(INC), .cout(adder_1_cout));
  and and_1 (and_1_out, INC, not_1_out);
  not not_1 (not_1_out, LD);
  Multiplexer #(.width(12)) multiplexer_1 (
    .in0(controlled_buffer_1_out), .in1(adder_1_out), .out(multiplexer_1_out), .sel(and_1_out));  // open: en
  Register #(.width(12)) register_1 (.D(multiplexer_1_out), .Q(OUTPUT), .clk(CLK), .clr(and_2_out));  // open: en
  and and_2 (and_2_out, not_3_out, not_2_out, CLR);
  not not_2 (not_2_out, LD);
  not not_3 (not_3_out, INC);
endmodule
