// Logisim project simplecomputer.circ as structural Verilog: 3 circuits, main circuit main
// LD
module main (
  input  in_1,
  input  in_2,
  input  in_3,
  input  in_4,
  output [1:0] out_5
);

  Priority_Encoder #(.select(2)) priority_encoder_1 (
    .in0(in_1), .in1(in_2), .in2(in_3), .in3(in_4), .out(out_5));  // open: gs, en_out, en_in
endmodule

module project2 (
  input  [7:0] in_1,
  input  in_2,
  input  in_3,
  input  SC_Clear,
  output [15:0] out_5,
  output [15:0] out_6,
  output [7:0] out_7
);

  wire clock_1_out, control_unit_1_in_veya_ac, control_unit_1_r_2, control_unit_1_read, control_unit_1_write,
       decoder_1_out0, decoder_1_out1, decoder_1_out2, decoder_2_out0, decoder_2_out1, decoder_2_out2,
       decoder_2_out3, nor_1_out, test_1_e;
  wire [1:0] control_unit_1_b1_b0, control_unit_1_c1_c0, control_unit_1_d1_d0, control_unit_1_s1_s0,
       control_unit_1_s3_s2;
  wire [2:0] IR_output_2;
  wire [3:0] Cnt_q;
  wire [7:0] bit_extender_5_out, decoder_4_out0, INPUT_output, register_1_q, test_1_ccr_out;
  wire [8:0] control_unit_1_clear, control_unit_1_inc, control_unit_1_load;
  wire [11:0] AR_output, bit_extender_1_out, bit_extender_2_out, bit_extender_3_out, bit_extender_4_out,
       IR_output, PC_output, SP_output;
  wire [15:0] AC_output, bit_extender_6_out, bit_extender_7_out, bit_extender_8_out, bit_extender_9_out,
       controlled_buffer_1_out, decoder_3_out0, DR_output, multiplexer_1_out, multiplexer_2_out, ram_1_data,
       TR_output;
  wire [15:15] IR_output_3;

  Multiplexer #(.select(2), .width(16)) multiplexer_1 (
    .in0(ram_1_data), .in1(controlled_buffer_1_out), .in2(out_5), .out(multiplexer_1_out),
    .sel(control_unit_1_b1_b0));  // open: in3, en
  Clock clock_1 (.out(clock_1_out));
  Bit_Extender #(.in_width(16), .out_width(12)) bit_extender_1 (.in(controlled_buffer_1_out), .out(bit_extender_1_out));
  Bit_Extender #(.in_width(16), .out_width(12)) bit_extender_2 (.in(multiplexer_1_out), .out(bit_extender_2_out));
  Bit_Extender #(.in_width(16), .out_width(12)) bit_extender_3 (.in(multiplexer_1_out), .out(bit_extender_3_out));
  Bit_Extender #(.in_width(16), .out_width(12)) bit_extender_4 (.in(multiplexer_1_out), .out(bit_extender_4_out));
  Bit_Extender #(.in_width(16), .out_width(8)) bit_extender_5 (.in(multiplexer_1_out), .out(bit_extender_5_out));
  _12bitReg_main PC (
    .INPUT(bit_extender_2_out), .CLK(clock_1_out), .INC(control_unit_1_inc[0]), .LD(control_unit_1_load[0]),
    .CLR(control_unit_1_clear[0]), .OUTPUT(PC_output));
  _12bitReg_main AR (
    .INPUT(bit_extender_3_out), .CLK(clock_1_out), .INC(control_unit_1_inc[1]), .LD(control_unit_1_load[1]),
    .CLR(control_unit_1_clear[1]), .OUTPUT(AR_output));
  _12bitReg_main SP (
    .INPUT(bit_extender_4_out), .CLK(clock_1_out), .INC(control_unit_1_inc[2]), .LD(control_unit_1_load[2]),
    .CLR(control_unit_1_clear[2]), .OUTPUT(SP_output));
  _16bitReg_main DR (
    .INPUT(multiplexer_1_out), .CLK(clock_1_out), .INC(control_unit_1_inc[3]), .LD(control_unit_1_load[3]),
    .CLR(control_unit_1_clear[3]), .OUTPUT(DR_output));
  _8bitReg_main INPUT (
    .INPUT(in_1), .CLK(clock_1_out), .INC(control_unit_1_inc[4]), .LD(control_unit_1_load[4]),
    .CLR(control_unit_1_clear[4]), .OUTPUT(INPUT_output));
  _16bitReg_main AC (
    .INPUT(out_6), .CLK(clock_1_out), .INC(control_unit_1_inc[5]), .LD(control_unit_1_load[5]),
    .CLR(control_unit_1_clear[5]), .OUTPUT(AC_output));
  _16bitReg_main IR (
    .INPUT(multiplexer_1_out), .CLK(clock_1_out), .INC(control_unit_1_inc[6]), .LD(control_unit_1_load[6]),
    .CLR(control_unit_1_clear[6]), .OUTPUT({IR_output_3[15], IR_output_2, IR_output}));
  _16bitReg_main TR (
    .INPUT(multiplexer_1_out), .CLK(clock_1_out), .INC(control_unit_1_inc[7]), .LD(control_unit_1_load[7]),
    .CLR(control_unit_1_clear[7]), .OUTPUT(TR_output));
  RAM #(.addrWidth(12), .dataWidth(16), .bus("separate")) ram_1 (
    .addr(bit_extender_1_out), .din(multiplexer_1_out), .data(ram_1_data), .str(control_unit_1_write),
    .clk(clock_1_out), .ld(control_unit_1_read));  // open: sel, clr
  assign bit_extender_6_out = {{8{1'b0}}, INPUT_output};  // Bit_Extender bit_extender_6
  Multiplexer #(.width(16)) multiplexer_2 (
    .in0(bit_extender_6_out), .in1(AC_output), .out(multiplexer_2_out), .sel(control_unit_1_in_veya_ac));  // open: en
  _8bitReg_main OUTPUT (
    .INPUT(bit_extender_5_out), .CLK(clock_1_out), .INC(control_unit_1_inc[8]), .LD(control_unit_1_load[8]),
    .CLR(control_unit_1_clear[8]), .OUTPUT(out_7));
  Decoder #(.select(2)) decoder_1 (
    .out0(decoder_1_out0), .out1(decoder_1_out1), .out2(decoder_1_out2), .sel(control_unit_1_c1_c0));  // open: out3, en
  assign bit_extender_7_out = {{4{1'b0}}, PC_output};  // Bit_Extender bit_extender_7
  assign controlled_buffer_1_out = decoder_1_out0 ? bit_extender_7_out : 16'bz;  // Controlled_Buffer controlled_buffer_1
  assign controlled_buffer_1_out = decoder_1_out1 ? bit_extender_8_out : 16'bz;  // Controlled_Buffer controlled_buffer_2
  assign bit_extender_8_out = {{4{1'b0}}, AR_output};  // Bit_Extender bit_extender_8
  assign controlled_buffer_1_out = decoder_1_out2 ? bit_extender_9_out : 16'bz;  // Controlled_Buffer controlled_buffer_3
  assign bit_extender_9_out = {{4{1'b0}}, SP_output};  // Bit_Extender bit_extender_9
  test test_1 (
    .CCR_IN(register_1_q), .in_2(DR_output), .in_3(multiplexer_2_out), .s1_s0(control_unit_1_s1_s0),
    .s3_s2(control_unit_1_s3_s2), .out_6(out_6), .CCR_OUT(test_1_ccr_out), .E(test_1_e));
  assign out_5 = decoder_2_out1 ? AC_output : 16'bz;  // Controlled_Buffer controlled_buffer_4
  assign out_5 = decoder_2_out2 ? {IR_output_3[15], IR_output_2, IR_output} : 16'bz;  // Controlled_Buffer controlled_buffer_5
  assign out_5 = decoder_2_out3 ? TR_output : 16'bz;  // Controlled_Buffer controlled_buffer_6
  assign out_5 = decoder_2_out0 ? DR_output : 16'bz;  // Controlled_Buffer controlled_buffer_7
  nor nor_1 (nor_1_out, AC_output[0], AC_output[1], AC_output[2], AC_output[3], AC_output[4], AC_output[5], AC_output[6], AC_output[7], AC_output[8], AC_output[9], AC_output[10], AC_output[11], AC_output[12], AC_output[13], AC_output[14], AC_output[15]);
  Decoder #(.select(2)) decoder_2 (
    .out0(decoder_2_out0), .out1(decoder_2_out1), .out2(decoder_2_out2), .out3(decoder_2_out3),
    .sel(control_unit_1_d1_d0));  // open: en
  Register register_1 (.D(test_1_ccr_out), .Q(register_1_q), .clk(clock_1_out));  // open: en, clr
  Hex_Digit_Display hex_digit_display_1 (.value(out_6[11:8]));  // open: dp
  Hex_Digit_Display hex_digit_display_2 (.value(out_6[15:12]));  // open: dp
  Counter #(.width(4), .max('hf)) Cnt (.Q(Cnt_q), .clk(clock_1_out), .clr(SC_Clear));  // open: load, D, count, carry
  Hex_Digit_Display hex_digit_display_3 (.value(out_6[7:4]));  // open: dp
  Decoder #(.select(4)) decoder_3 (
    .out0(decoder_3_out0[0]), .out1(decoder_3_out0[1]), .out2(decoder_3_out0[2]), .out3(decoder_3_out0[3]),
    .out4(decoder_3_out0[4]), .out5(decoder_3_out0[5]), .out6(decoder_3_out0[6]), .out7(decoder_3_out0[7]),
    .out8(decoder_3_out0[8]), .out9(decoder_3_out0[9]), .out10(decoder_3_out0[10]),
    .out11(decoder_3_out0[11]), .out12(decoder_3_out0[12]), .out13(decoder_3_out0[13]),
    .out14(decoder_3_out0[14]), .out15(decoder_3_out0[15]), .sel(Cnt_q));  // open: en
  Hex_Digit_Display hex_digit_display_4 (.value(out_6[3:0]));  // open: dp
  Decoder #(.select(3)) decoder_4 (
    .out0(decoder_4_out0[0]), .out1(decoder_4_out0[1]), .out2(decoder_4_out0[2]), .out3(decoder_4_out0[3]),
    .out4(decoder_4_out0[4]), .out5(decoder_4_out0[5]), .out6(decoder_4_out0[6]), .out7(decoder_4_out0[7]),
    .sel(IR_output_2));  // open: en
  Control_Unit control_unit_1 (
    .IR_0_11(IR_output), .D(decoder_4_out0), .T(decoder_3_out0), .I(IR_output_3[15]), .E(test_1_e),
    .R(control_unit_1_r_2), .AC15(AC_output[15]), .AC0(AC_output[0]), .FGI(in_3), .FGO(in_2),
    .AC_Flag(nor_1_out), .Inc(control_unit_1_inc), .Load(control_unit_1_load), .Clear(control_unit_1_clear),
    .Read(control_unit_1_read), .Write(control_unit_1_write), .B1_B0(control_unit_1_b1_b0),
    .C1_C0(control_unit_1_c1_c0), .D1_D0(control_unit_1_d1_d0), .S3_S2(control_unit_1_s3_s2),
    .S1_S0(control_unit_1_s1_s0), .IN_veya_AC(control_unit_1_in_veya_ac), .R_2(control_unit_1_r_2));  // open: SC
endmodule

// CU
module Control_Unit (
  input  [11:0] IR_0_11,
  input  [7:0] D,
  input  [15:0] T,
  input  I,
  input  E,
  input  R,
  input  AC15,
  input  AC0,
  input  FGI,
  input  FGO,
  input  AC_Flag,
  output [8:0] Inc,
  output [8:0] Load,
  output [8:0] Clear,
  output Read,
  output Write,
  output [1:0] B1_B0,
  output [1:0] C1_C0,
  output [1:0] D1_D0,
  output [1:0] S3_S2,
  output [1:0] S1_S0,
  output IN_veya_AC,
  output R_2,
  output SC
);

  wire D0T2I_prime_out, D0T3I_prime_out, D1T2I_prime_out, D1T3I_prime_out, D2T2I_prime_out, D2T3I_prime_out,
       D3T2I_prime_out, D3T3I_prime_out, D4T2I_prime_out, D4T3I_prime_out, D5T2I_prime_out, D5T3I_prime_out,
       D6T2I_prime_out, D6T3I_prime_out, not_1_out, not_2_out, not_3_out, not_4_out, not_5_out, not_6_out,
       not_7_out, not_8_out, not_9_out, not_10_out, not_11_out, not_12_out, not_13_out, not_14_out,
       not_15_out, not_16_out, or_30_out, or_31_out, or_32_out, or_33_out, or_34_out, or_35_out, or_36_out,
       or_37_out, or_38_out, or_39_out, or_40_out, or_41_out, or_42_out, or_43_out, or_44_out, or_45_out,
       or_46_out, or_47_out, or_48_out, or_49_out, or_50_out, or_51_out, or_52_out, or_53_out, or_54_out,
       R_prime_T0_out, R_prime_T1_out, RT0_out, RT1_out, RT2_out, T2B0_out, T2B1_out, T2B2_out, T2B3_out,
       T2B4_out, T2B5_out, T2B6_2_out, T2B6_out, T2B7_2_out, T2B7_out, T2B8_2_out, T2B8_out, T2B9_2_out,
       T2B9_out, T2B10_2_out, T2B10_out, T2B11_2_out, T2B11_out, T3B6_out, T3B7_out, T3B9_out;

  not not_1 (not_1_out, AC15);
  not not_2 (not_2_out, I);
  not not_3 (not_3_out, E);
  not not_4 (not_4_out, D[7]);
  not not_5 (not_5_out, not_1_out);
  and T2B11 (T2B11_out, D[7], not_2_out, not_4_out, T[2], IR_0_11[11]);
  and T2B10 (T2B10_out, D[7], not_2_out, not_4_out, T[2], IR_0_11[10]);
  and T2B9 (T2B9_out, D[7], not_2_out, not_4_out, T[2], IR_0_11[9]);
  and T2B8 (T2B8_out, D[7], not_2_out, not_4_out, T[2], IR_0_11[8]);
  and T2B7 (T2B7_out, D[7], not_2_out, not_4_out, T[2], IR_0_11[7]);
  and T2B6 (T2B6_out, D[7], not_2_out, not_4_out, T[2], IR_0_11[6]);
  and T2B5 (T2B5_out, D[7], not_2_out, not_4_out, T[2], IR_0_11[5]);
  and T2B11_2 (T2B11_2_out, D[7], T[2], not_4_out, I, IR_0_11[11]);
  and T2B9_2 (T2B9_2_out, FGI, D[7], T[2], not_4_out, I, IR_0_11[9]);
  and T2B7_2 (T2B7_2_out, D[7], T[2], not_4_out, I, IR_0_11[7]);
  and D0T2I_prime (D0T2I_prime_out, T[3], not_4_out, D[0], not_2_out);
  and D1T2I_prime (D1T2I_prime_out, T[3], not_4_out, D[1], not_2_out);
  and D2T2I_prime (D2T2I_prime_out, T[3], not_4_out, D[2], not_2_out);
  and D3T2I_prime (D3T2I_prime_out, T[3], not_4_out, D[3], not_2_out);
  and D4T2I_prime (D4T2I_prime_out, T[3], not_4_out, D[4], not_2_out);
  and D5T2I_prime (D5T2I_prime_out, T[3], not_4_out, D[5], not_2_out);
  and D6T2I_prime (D6T2I_prime_out, T[3], not_4_out, D[6], not_2_out);
  and T3B9 (T3B9_out, not_2_out, D[7], not_4_out, IR_0_11[9], T[3]);
  and T3B7 (T3B7_out, not_2_out, D[7], not_4_out, IR_0_11[7], T[3]);
  and T3B6 (T3B6_out, not_2_out, D[7], not_4_out, IR_0_11[6], T[3]);
  and D0T3I_prime (D0T3I_prime_out, T[3], not_4_out, D[0], not_2_out);
  and D1T3I_prime (D1T3I_prime_out, T[3], not_4_out, D[1], not_2_out);
  and D2T3I_prime (D2T3I_prime_out, T[3], not_4_out, D[2], not_2_out);
  and D3T3I_prime (D3T3I_prime_out, T[3], not_4_out, D[3], not_2_out);
  and D4T3I_prime (D4T3I_prime_out, T[3], not_4_out, D[4], not_2_out);
  and D5T3I_prime (D5T3I_prime_out, T[3], not_4_out, D[5], not_2_out);
  and D6T3I_prime (D6T3I_prime_out, T[3], not_4_out, D[6], not_2_out);
  and R_prime_T0 (R_prime_T0_out, T[0], not_4_out);
  and R_prime_T1 (R_prime_T1_out, not_4_out, T[1]);
  and RT0 (RT0_out, D[7], T[0]);
  and RT1 (RT1_out, D[7], T[1]);
  and RT2 (RT2_out, D[7], T[2]);
  and T2B4 (T2B4_out, D[7], not_2_out, not_4_out, T[2], IR_0_11[4], not_1_out);
  and T2B0 (T2B0_out, D[7], not_2_out, not_4_out, T[2], IR_0_11[0]);
  and T2B10_2 (T2B10_2_out, D[7], T[2], not_4_out, I, IR_0_11[10]);
  and T2B8_2 (T2B8_2_out, D[7], T[2], not_4_out, I, IR_0_11[8], FGO);
  and T2B6_2 (T2B6_2_out, D[7], T[2], not_4_out, I, IR_0_11[6]);
  and T2B3 (T2B3_out, D[7], not_2_out, not_4_out, T[2], IR_0_11[3], not_5_out);
  and T2B2 (T2B2_out, D[7], not_2_out, not_4_out, T[2], IR_0_11[2], AC_Flag);
  and T2B1 (T2B1_out, D[7], not_2_out, not_4_out, T[2], IR_0_11[1], not_3_out);
  not not_6 (not_6_out, 1'b1);
  not not_7 (not_7_out, 1'b1);
  not not_8 (not_8_out, 1'b1);
  not not_9 (not_9_out, 1'b1);
  not not_10 (not_10_out, 1'b1);
  or or_1 (Load[3], D6T2I_prime_out, T2B9_out, T2B7_out, D0T2I_prime_out, T2B6_out, D1T2I_prime_out, D2T2I_prime_out);
  or or_2 (Load[5], D1T2I_prime_out, T3B9_out, T3B7_out, T3B6_out, T2B11_2_out, D0T2I_prime_out, D2T2I_prime_out);
  not not_11 (not_11_out, 1'b1);
  or or_3 (Inc[0], T2B8_2_out, T2B4_out, T2B3_out, T2B2_out, T2B9_2_out, T2B1_out, R_prime_T1_out, RT2_out);
  buf or_4 (Inc[1], D5T3I_prime_out);  // OR_Gate
  buf or_5 (Inc[2], not_6_out);  // OR_Gate
  buf or_6 (Inc[3], not_7_out);  // OR_Gate
  buf or_7 (Inc[4], not_8_out);  // OR_Gate
  or or_8 (Inc[5], T2B5_out, not_9_out);
  buf or_9 (Inc[6], not_9_out);  // OR_Gate
  buf or_10 (Inc[7], not_9_out);  // OR_Gate
  buf or_11 (Inc[8], not_9_out);  // OR_Gate
  buf or_12 (Load[0], D4T2I_prime_out);  // OR_Gate
  buf or_13 (Load[1], R_prime_T1_out);  // OR_Gate
  buf or_14 (Load[2], not_10_out);  // OR_Gate
  buf or_15 (Load[4], not_10_out);  // OR_Gate
  buf or_16 (Load[6], R_prime_T0_out);  // OR_Gate
  buf or_17 (Load[7], RT0_out);  // OR_Gate
  buf or_18 (Load[8], T2B10_2_out);  // OR_Gate
  buf or_19 (Clear[0], RT1_out);  // OR_Gate
  buf or_20 (Clear[1], RT0_out);  // OR_Gate
  buf or_21 (Clear[2], not_11_out);  // OR_Gate
  buf or_22 (Clear[3], not_11_out);  // OR_Gate
  buf or_23 (Clear[4], not_11_out);  // OR_Gate
  buf or_24 (Clear[5], T2B11_out);  // OR_Gate
  buf or_25 (Clear[6], not_11_out);  // OR_Gate
  buf or_26 (Clear[7], not_11_out);  // OR_Gate
  buf or_27 (Clear[8], not_11_out);  // OR_Gate
  or or_28 (Read, D0T2I_prime_out, D1T2I_prime_out, D2T2I_prime_out, R_prime_T0_out, D6T2I_prime_out);
  or or_29 (Write, D3T2I_prime_out, D5T3I_prime_out, RT1_out);
  not not_12 (not_12_out, 1'b1);
  not not_13 (not_13_out, 1'b1);
  not not_14 (not_14_out, 1'b1);
  not not_15 (not_15_out, 1'b1);
  not not_16 (not_16_out, 1'b1);
  or or_30 (or_30_out, D0T2I_prime_out, D1T2I_prime_out, D2T2I_prime_out, R_prime_T0_out, D6T2I_prime_out);
  or or_31 (or_31_out, D4T2I_prime_out, RT0_out, D5T2I_prime_out);
  or or_32 (or_32_out, RT1_out, T2B9_out, T2B7_out, T2B6_out, T2B10_2_out, D3T2I_prime_out, R_prime_T1_out);
  buf or_33 (or_33_out, not_12_out);  // OR_Gate
  or or_34 (or_34_out, R_prime_T0_out, D5T2I_prime_out, RT0_out);
  or or_35 (or_35_out, D5T3I_prime_out, D0T2I_prime_out, D1T2I_prime_out, D2T2I_prime_out, D4T2I_prime_out, D6T2I_prime_out, D3T2I_prime_out, RT1_out);
  buf or_36 (or_36_out, not_13_out);  // OR_Gate
  buf or_37 (or_37_out, not_13_out);  // OR_Gate
  buf or_38 (or_38_out, not_14_out);  // OR_Gate
  or or_39 (or_39_out, T2B9_out, T2B7_out, T2B6_out, T2B10_2_out, D3T2I_prime_out);
  buf or_40 (or_40_out, R_prime_T1_out);  // OR_Gate
  buf or_41 (or_41_out, RT1_out);  // OR_Gate
  or or_42 (or_42_out, T3B7_out, T3B6_out);
  or or_43 (or_43_out, T3B9_out, D0T2I_prime_out);
  or or_44 (or_44_out, T2B11_2_out, D1T2I_prime_out, D2T2I_prime_out);
  buf or_45 (or_45_out, not_15_out);  // OR_Gate
  or or_46 (or_46_out, T3B7_out, T2B11_2_out, D0T2I_prime_out, D2T2I_prime_out);
  or or_47 (or_47_out, T3B6_out, D1T2I_prime_out);
  buf or_48 (or_48_out, not_16_out);  // OR_Gate
  buf or_49 (or_49_out, T3B9_out);  // OR_Gate
  buf or_50 (or_50_out, T2B11_2_out);  // OR_Gate
  or or_51 (or_51_out, D0T2I_prime_out, D1T2I_prime_out);
  or or_52 (or_52_out, T2B6_2_out, RT2_out);
  buf or_53 (or_53_out, T2B7_2_out);  // OR_Gate
  buf or_54 (or_54_out, RT2_out);  // OR_Gate
  Priority_Encoder #(.select(2)) priority_encoder_1 (
    .in0(or_30_out), .in1(or_31_out), .in2(or_32_out), .in3(or_33_out), .out(B1_B0));  // open: gs, en_out, en_in
  Priority_Encoder #(.select(2)) priority_encoder_2 (
    .in0(or_34_out), .in1(or_35_out), .in2(or_36_out), .in3(or_37_out), .out(C1_C0));  // open: gs, en_out, en_in
  Priority_Encoder #(.select(2)) priority_encoder_3 (
    .in0(or_38_out), .in1(or_39_out), .in2(or_40_out), .in3(or_41_out), .out(D1_D0));  // open: gs, en_out, en_in
  Priority_Encoder #(.select(2)) priority_encoder_4 (
    .in0(or_42_out), .in1(or_43_out), .in2(or_44_out), .in3(or_45_out), .out(S3_S2));  // open: gs, en_out, en_in
  Priority_Encoder #(.select(2)) priority_encoder_5 (
    .in0(or_46_out), .in1(or_47_out), .in2(or_48_out), .in3(or_49_out), .out(S1_S0));  // open: gs, en_out, en_in
  Priority_Encoder #(.select(1)) priority_encoder_6 (
    .in0(or_50_out), .in1(or_51_out), .out(IN_veya_AC));  // open: gs, en_out, en_in
  Priority_Encoder #(.select(1)) priority_encoder_7 (.in0(or_52_out), .in1(or_53_out));  // open: out, gs, en_out, en_in
  Priority_Encoder #(.select(1)) priority_encoder_8 (.in0(or_54_out), .out(SC));  // open: in1, gs, en_out, en_in
  not not_17 (R_2, 1'b1);

  assign R = D[7];

  // Notes on the sheet:
  //   pc halt,sonra yap
endmodule
