// Logisim project project-final.circ as structural Verilog: 14 circuits, main circuit main
module main (
  input  Cin,
  input  a0,
  input  b0,
  input  a1,
  input  b1,
  input  a2,
  input  b2,
  input  a3,
  input  b3,
  input  a4,
  input  b4,
  input  a5,
  input  b5,
  input  a6,
  input  b6,
  input  a7,
  input  b7,
  input  a8,
  input  b8,
  input  a9,
  input  b9,
  input  a10,
  input  b10,
  input  a11,
  input  b11,
  input  a12,
  input  b12,
  input  a13,
  input  b13,
  input  a14,
  input  b14,
  input  a15,
  input  b15,
  input  [1:0] s1_s0,
  input  [1:0] s3_s2,
  output C,
  output O,
  output N,
  output Z,
  output f0,
  output f1,
  output f2,
  output f3,
  output f4,
  output f5,
  output f6,
  output f7,
  output f8,
  output f9,
  output f10,
  output f11,
  output f12,
  output f13,
  output f14,
  output f15,
  output Cout
);

  wire alu_complete_1_i_2, alu_complete_1_r_4, alu_complete_1_r_5, alu_complete_1_r_6, register_8bit_1_c_2,
       register_8bit_1_i_2, register_8bit_1_n_2, register_8bit_1_o_2, register_8bit_1_r_3,
       register_8bit_1_r_4, register_8bit_1_r_out, register_8bit_1_z_2;

  Register_8bit register_8bit_1 (
    .R_in(alu_complete_1_r_4), .R(alu_complete_1_r_5), .R_2(alu_complete_1_r_6), .I(alu_complete_1_i_2),
    .Z(Z), .N(N), .O(O), .C(C), .R_out(register_8bit_1_r_out), .R_3(register_8bit_1_r_3),
    .R_4(register_8bit_1_r_4), .I_2(register_8bit_1_i_2), .Z_2(register_8bit_1_z_2),
    .N_2(register_8bit_1_n_2), .O_2(register_8bit_1_o_2), .C_2(register_8bit_1_c_2));
  ALU_Complete alu_complete_1 (
    .Cin(Cin), .a0(a0), .b0(b0), .a1(a1), .b1(b1), .a2(a2), .b2(b2), .a3(a3), .b3(b3), .a4(a4), .b4(b4),
    .a5(a5), .b5(b5), .a6(a6), .b6(b6), .a7(a7), .b7(b7), .a8(a8), .b8(b8), .a9(a9), .b9(b9), .a10(a10),
    .b10(b10), .a11(a11), .b11(b11), .a12(a12), .b12(b12), .a13(a13), .b13(b13), .a14(a14), .b14(b14),
    .a15(a15), .b15(b15), .s1_s0(s1_s0), .s3_s2(s3_s2), .R(register_8bit_1_r_out), .R_2(register_8bit_1_r_3),
    .R_3(register_8bit_1_r_4), .I(register_8bit_1_i_2), .Z(register_8bit_1_z_2), .N(register_8bit_1_n_2),
    .O(register_8bit_1_o_2), .C(register_8bit_1_c_2), .Z_Flag(Z), .N_Flag(N), .O_Flag(O), .C_Flag(C),
    .f0(f0), .f1(f1), .f2(f2), .f3(f3), .f4(f4), .f5(f5), .f6(f6), .f7(f7), .f8(f8), .f9(f9), .f10(f10),
    .f11(f11), .f12(f12), .f13(f13), .f14(f14), .f15(f15), .Cout(Cout), .R_4(alu_complete_1_r_4),
    .R_5(alu_complete_1_r_5), .R_6(alu_complete_1_r_6), .I_2(alu_complete_1_i_2));

  // Notes on the sheet:
  //   Test Aşamalrı bittikten sonra , teslim etmeden önce Cin ayarlaması yapılamsı gerekiyor.
endmodule

// aritmatic
module Aritmatik_unit_1b (
  input  Cin,
  input  A,
  input  B,
  input  [1:0] Cntr,
  output F,
  output Cout
);

  wire multiplexer_1_out, not_1_out, not_2_out;

  not not_1 (not_1_out, 1'b1);
  not not_2 (not_2_out, B);
  Multiplexer #(.select(2), .enable("false")) multiplexer_1 (
    .in0(not_1_out), .in1(B), .in2(not_2_out), .in3(1'b1), .out(multiplexer_1_out), .sel(Cntr));
  Adder #(.width(1)) adder_1 (.a(A), .b(multiplexer_1_out), .out(F), .cin(Cin), .cout(Cout));
endmodule

// logic
module logic_unit_1b (
  input  A,
  input  B,
  input  [1:0] Cnt,
  input  Cin,
  output Out
);

  wire and_1_out, multiplexer_1_out, multiplexer_2_out, nand_1_out, nor_1_out, not_1_out, not_2_out,
       or_1_out, xnor_1_out, xor_1_out;

  not not_1 (not_1_out, A);
  nand nand_1 (nand_1_out, A, B);
  not not_2 (not_2_out, A);
  and and_1 (and_1_out, A, B);
  xor xor_1 (xor_1_out, A, B);
  or or_1 (or_1_out, A, B);
  xnor xnor_1 (xnor_1_out, A, B);
  nor nor_1 (nor_1_out, A, B);
  Multiplexer #(.select(2), .enable("false")) multiplexer_1 (
    .in0(and_1_out), .in1(xor_1_out), .in2(or_1_out), .in3(not_1_out), .out(multiplexer_1_out), .sel(Cnt));
  Multiplexer #(.select(2), .enable("false")) multiplexer_2 (
    .in0(nand_1_out), .in1(xnor_1_out), .in2(nor_1_out), .in3(not_2_out), .out(multiplexer_2_out), .sel(Cnt));
  Multiplexer #(.enable("false")) multiplexer_3 (
    .in0(multiplexer_1_out), .in1(multiplexer_2_out), .out(Out), .sel(Cin));
endmodule

// Alu-1
module Alu_1b (
  input  CinForLogic,
  input  A,
  input  B,
  input  CinForArithmetic,
  input  [1:0] s1_s0,
  input  [1:0] s3_s2,
  output Cout,
  output Out
);

  wire aritmatik_unit_1b_1_f, logic_unit_1b_1_out;

  Aritmatik_unit_1b aritmatik_unit_1b_1 (
    .Cin(CinForArithmetic), .A(A), .B(B), .Cntr(s1_s0), .F(aritmatik_unit_1b_1_f), .Cout(Cout));
  logic_unit_1b logic_unit_1b_1 (.A(A), .B(B), .Cnt(s1_s0), .Cin(CinForLogic), .Out(logic_unit_1b_1_out));
  Multiplexer #(.select(2), .enable("false")) multiplexer_1 (
    .in1(logic_unit_1b_1_out), .in2(aritmatik_unit_1b_1_f), .out(Out), .sel(s3_s2));  // open: in0, in3
endmodule

module Alu_16b (
  input  Cin,
  input  a0,
  input  b0,
  input  a1,
  input  b1,
  input  a2,
  input  b2,
  input  a3,
  input  b3,
  input  a4,
  input  b4,
  input  a5,
  input  b5,
  input  a6,
  input  b6,
  input  a7,
  input  b7,
  input  a8,
  input  b8,
  input  a9,
  input  b9,
  input  a10,
  input  b10,
  input  a11,
  input  b11,
  input  a12,
  input  b12,
  input  a13,
  input  b13,
  input  a14,
  input  b14,
  input  a15,
  input  b15,
  input  [1:0] s1_s0,
  input  [1:0] s3_s2,
  output Z_flag,
  output N_Flag,
  output O_Flag,
  output C_flag,
  output f0,
  output f1,
  output f2,
  output f3,
  output f4,
  output f5,
  output f6,
  output f7,
  output f8,
  output f9,
  output f10,
  output f11,
  output f12,
  output f13,
  output f14,
  output f15,
  output Cout
);

  wire _1_2_cout, _1_3_cout, _1_4_cout, _1_5_cout, _1_6_cout, _1_7_cout, _1_8_cout, _1_cout, _2_2_cout,
       _2_3_cout, _2_4_cout, _2_5_cout, _2_6_cout, _2_7_cout, _2_cout;

  Alu_1b _1 (
    .CinForLogic(Cin), .A(a0), .B(b0), .CinForArithmetic(Cin), .s1_s0(s1_s0), .s3_s2(s3_s2), .Cout(_1_cout),
    .Out(f0));
  Alu_1b _2 (
    .CinForLogic(Cin), .A(a1), .B(b1), .CinForArithmetic(_1_cout), .s1_s0(s1_s0), .s3_s2(s3_s2),
    .Cout(_2_cout), .Out(f1));
  Alu_1b _1_2 (
    .CinForLogic(Cin), .A(a2), .B(b2), .CinForArithmetic(_2_cout), .s1_s0(s1_s0), .s3_s2(s3_s2),
    .Cout(_1_2_cout), .Out(f2));
  Alu_1b _2_2 (
    .CinForLogic(Cin), .A(a3), .B(b3), .CinForArithmetic(_1_2_cout), .s1_s0(s1_s0), .s3_s2(s3_s2),
    .Cout(_2_2_cout), .Out(f3));
  Alu_1b _1_3 (
    .CinForLogic(Cin), .A(a4), .B(b4), .CinForArithmetic(_2_2_cout), .s1_s0(s1_s0), .s3_s2(s3_s2),
    .Cout(_1_3_cout), .Out(f4));
  Alu_1b _2_3 (
    .CinForLogic(Cin), .A(a5), .B(b5), .CinForArithmetic(_1_3_cout), .s1_s0(s1_s0), .s3_s2(s3_s2),
    .Cout(_2_3_cout), .Out(f5));
  Alu_1b _1_4 (
    .CinForLogic(Cin), .A(a6), .B(b6), .CinForArithmetic(_2_3_cout), .s1_s0(s1_s0), .s3_s2(s3_s2),
    .Cout(_1_4_cout), .Out(f6));
  Alu_1b _2_4 (
    .CinForLogic(Cin), .A(a7), .B(b7), .CinForArithmetic(_1_4_cout), .s1_s0(s1_s0), .s3_s2(s3_s2),
    .Cout(_2_4_cout), .Out(f7));
  Alu_1b _1_5 (
    .CinForLogic(Cin), .A(a8), .B(b8), .CinForArithmetic(_2_4_cout), .s1_s0(s1_s0), .s3_s2(s3_s2),
    .Cout(_1_5_cout), .Out(f8));
  Alu_1b _2_5 (
    .CinForLogic(Cin), .A(a9), .B(b9), .CinForArithmetic(_1_5_cout), .s1_s0(s1_s0), .s3_s2(s3_s2),
    .Cout(_2_5_cout), .Out(f9));
  Alu_1b _1_6 (
    .CinForLogic(Cin), .A(a10), .B(b10), .CinForArithmetic(_2_5_cout), .s1_s0(s1_s0), .s3_s2(s3_s2),
    .Cout(_1_6_cout), .Out(f10));
  Alu_1b _2_6 (
    .CinForLogic(Cin), .A(a11), .B(b11), .CinForArithmetic(_1_6_cout), .s1_s0(s1_s0), .s3_s2(s3_s2),
    .Cout(_2_6_cout), .Out(f11));
  Alu_1b _1_7 (
    .CinForLogic(Cin), .A(a12), .B(b12), .CinForArithmetic(_2_6_cout), .s1_s0(s1_s0), .s3_s2(s3_s2),
    .Cout(_1_7_cout), .Out(f12));
  Alu_1b _2_7 (
    .CinForLogic(Cin), .A(a13), .B(b13), .CinForArithmetic(_1_7_cout), .s1_s0(s1_s0), .s3_s2(s3_s2),
    .Cout(_2_7_cout), .Out(f13));
  Alu_1b _1_8 (
    .CinForLogic(Cin), .A(a14), .B(b14), .CinForArithmetic(_2_7_cout), .s1_s0(s1_s0), .s3_s2(s3_s2),
    .Cout(_1_8_cout), .Out(f14));
  Alu_1b _2_8 (
    .CinForLogic(Cin), .A(a15), .B(b15), .CinForArithmetic(_1_8_cout), .s1_s0(s1_s0), .s3_s2(s3_s2),
    .Cout(C_flag), .Out(f15));
  nor nor_1 (Z_flag, f0, f1, f2, f3, f4, f5, f6, f7, f8, f9, f10, f11, f12, f13, f14, f15);
  xor xor_1 (O_Flag, C_flag, _1_8_cout);

  assign Cout = C_flag;
  assign N_Flag = f15;
endmodule

module Arit_Right_S (
  input  a15,
  input  a14,
  input  a13,
  input  a12,
  input  a11,
  input  a10,
  input  a9,
  input  a8,
  input  a7,
  input  a6,
  input  a5,
  input  a4,
  input  a3,
  input  a2,
  input  a1,
  input  a0,
  output f15,
  output f14,
  output f13,
  output f12,
  output f11,
  output f10,
  output f9,
  output f8,
  output f7,
  output f6,
  output f5,
  output f4,
  output f3,
  output f2,
  output f1,
  output f0
);


  assign f0 = a1;
  assign f1 = a2;
  assign f2 = a3;
  assign f3 = a4;
  assign f4 = a5;
  assign f5 = a6;
  assign f6 = a7;
  assign f7 = a8;
  assign f8 = a9;
  assign f9 = a10;
  assign f10 = a11;
  assign f11 = a12;
  assign f12 = a13;
  assign f13 = a14;
  assign f14 = a15;
  assign f15 = a15;
endmodule

module CircularShift (
  input  a15,
  input  a14,
  input  a13,
  input  a12,
  input  a11,
  input  a10,
  input  a9,
  input  a8,
  input  a7,
  input  a6,
  input  a5,
  input  a4,
  input  a3,
  input  a2,
  input  a1,
  input  a0,
  input  Cin,
  output f15,
  output f14,
  output f13,
  output f12,
  output f11,
  output f10,
  output f9,
  output f8,
  output f7,
  output f6,
  output f5,
  output f4,
  output f3,
  output f2,
  output f1,
  output f0
);

  Multiplexer #(.enable("false")) multiplexer_1 (.in0(a0), .in1(a14), .out(f15), .sel(Cin));
  Multiplexer #(.enable("false")) multiplexer_2 (.in0(a15), .in1(a13), .out(f14), .sel(Cin));
  Multiplexer #(.enable("false")) multiplexer_3 (.in0(a14), .in1(a12), .out(f13), .sel(Cin));
  Multiplexer #(.enable("false")) multiplexer_4 (.in0(a13), .in1(a11), .out(f12), .sel(Cin));
  Multiplexer #(.enable("false")) multiplexer_5 (.in0(a12), .in1(a10), .out(f11), .sel(Cin));
  Multiplexer #(.enable("false")) multiplexer_6 (.in0(a11), .in1(a9), .out(f10), .sel(Cin));
  Multiplexer #(.enable("false")) multiplexer_7 (.in0(a10), .in1(a8), .out(f9), .sel(Cin));
  Multiplexer #(.enable("false")) multiplexer_8 (.in0(a9), .in1(a7), .out(f8), .sel(Cin));
  Multiplexer #(.enable("false")) multiplexer_9 (.in0(a8), .in1(a6), .out(f7), .sel(Cin));
  Multiplexer #(.enable("false")) multiplexer_10 (.in0(a7), .in1(a5), .out(f6), .sel(Cin));
  Multiplexer #(.enable("false")) multiplexer_11 (.in0(a6), .in1(a4), .out(f5), .sel(Cin));
  Multiplexer #(.enable("false")) multiplexer_12 (.in0(a5), .in1(a3), .out(f4), .sel(Cin));
  Multiplexer #(.enable("false")) multiplexer_13 (.in0(a4), .in1(a2), .out(f3), .sel(Cin));
  Multiplexer #(.enable("false")) multiplexer_14 (.in0(a3), .in1(a1), .out(f2), .sel(Cin));
  Multiplexer #(.enable("false")) multiplexer_15 (.in0(a2), .in1(a0), .out(f1), .sel(Cin));
  Multiplexer #(.enable("false")) multiplexer_16 (.in0(a1), .in1(a15), .out(f0), .sel(Cin));

  // Notes on the sheet:
  //   0-Right Shift,1-Left Shift
endmodule

module LogicShift (
  input  a15,
  input  a14,
  input  a13,
  input  a12,
  input  a11,
  input  a10,
  input  a9,
  input  a8,
  input  a7,
  input  a6,
  input  a5,
  input  a4,
  input  a3,
  input  a2,
  input  a1,
  input  a0,
  input  Cin,
  output f15,
  output f14,
  output f13,
  output f12,
  output f11,
  output f10,
  output f9,
  output f8,
  output f7,
  output f6,
  output f5,
  output f4,
  output f3,
  output f2,
  output f1,
  output f0
);

  wire not_1_out;

  not not_1 (not_1_out, 1'b1);
  Multiplexer #(.enable("false")) multiplexer_1 (.in0(not_1_out), .in1(a14), .out(f15), .sel(Cin));
  Multiplexer #(.enable("false")) multiplexer_2 (.in0(a15), .in1(a13), .out(f14), .sel(Cin));
  Multiplexer #(.enable("false")) multiplexer_3 (.in0(a14), .in1(a12), .out(f13), .sel(Cin));
  Multiplexer #(.enable("false")) multiplexer_4 (.in0(a13), .in1(a11), .out(f12), .sel(Cin));
  Multiplexer #(.enable("false")) multiplexer_5 (.in0(a12), .in1(a10), .out(f11), .sel(Cin));
  Multiplexer #(.enable("false")) multiplexer_6 (.in0(a11), .in1(a9), .out(f10), .sel(Cin));
  Multiplexer #(.enable("false")) multiplexer_7 (.in0(a10), .in1(a8), .out(f9), .sel(Cin));
  Multiplexer #(.enable("false")) multiplexer_8 (.in0(a9), .in1(a7), .out(f8), .sel(Cin));
  Multiplexer #(.enable("false")) multiplexer_9 (.in0(a8), .in1(a6), .out(f7), .sel(Cin));
  Multiplexer #(.enable("false")) multiplexer_10 (.in0(a7), .in1(a5), .out(f6), .sel(Cin));
  Multiplexer #(.enable("false")) multiplexer_11 (.in0(a6), .in1(a4), .out(f5), .sel(Cin));
  Multiplexer #(.enable("false")) multiplexer_12 (.in0(a5), .in1(a3), .out(f4), .sel(Cin));
  Multiplexer #(.enable("false")) multiplexer_13 (.in0(a4), .in1(a2), .out(f3), .sel(Cin));
  Multiplexer #(.enable("false")) multiplexer_14 (.in0(a3), .in1(a1), .out(f2), .sel(Cin));
  Multiplexer #(.enable("false")) multiplexer_15 (.in0(a2), .in1(a0), .out(f1), .sel(Cin));
  Multiplexer #(.enable("false")) multiplexer_16 (.in0(a1), .in1(not_1_out), .out(f0), .sel(Cin));

  // Notes on the sheet:
  //   0-Right Shift,1-Left Shift
endmodule

// shift
module ShiftOperation_16b (
  input  a15,
  input  a14,
  input  a13,
  input  a12,
  input  a11,
  input  a10,
  input  a9,
  input  a8,
  input  a7,
  input  a6,
  input  a5,
  input  a4,
  input  a3,
  input  a2,
  input  a1,
  input  a0,
  input  [1:0] s1_s0,
  input  Cin,
  output f15,
  output f14,
  output f13,
  output f12,
  output f11,
  output f10,
  output f9,
  output f8,
  output f7,
  output f6,
  output f5,
  output f4,
  output f3,
  output f2,
  output f1,
  output out_34
);

  wire arit_left_s_1_f0, arit_left_s_1_f1, arit_left_s_1_f2, arit_left_s_1_f3, arit_left_s_1_f4,
       arit_left_s_1_f5, arit_left_s_1_f6, arit_left_s_1_f7, arit_left_s_1_f8, arit_left_s_1_f9,
       arit_left_s_1_f10, arit_left_s_1_f11, arit_left_s_1_f12, arit_left_s_1_f13, arit_left_s_1_f14,
       arit_left_s_1_f15, arit_right_s_1_f0, arit_right_s_1_f1, arit_right_s_1_f2, arit_right_s_1_f3,
       arit_right_s_1_f4, arit_right_s_1_f5, arit_right_s_1_f6, arit_right_s_1_f7, arit_right_s_1_f8,
       arit_right_s_1_f9, arit_right_s_1_f10, arit_right_s_1_f11, arit_right_s_1_f12, arit_right_s_1_f13,
       arit_right_s_1_f14, arit_right_s_1_f15, circularshift_1_f0, circularshift_1_f1, circularshift_1_f2,
       circularshift_1_f3, circularshift_1_f4, circularshift_1_f5, circularshift_1_f6, circularshift_1_f7,
       circularshift_1_f8, circularshift_1_f9, circularshift_1_f10, circularshift_1_f11, circularshift_1_f12,
       circularshift_1_f13, circularshift_1_f14, circularshift_1_f15, logicshift_1_f0, logicshift_1_f1,
       logicshift_1_f2, logicshift_1_f3, logicshift_1_f4, logicshift_1_f5, logicshift_1_f6, logicshift_1_f7,
       logicshift_1_f8, logicshift_1_f9, logicshift_1_f10, logicshift_1_f11, logicshift_1_f12,
       logicshift_1_f13, logicshift_1_f14, logicshift_1_f15;

  LogicShift logicshift_1 (
    .a15(a15), .a14(a14), .a13(a13), .a12(a12), .a11(a11), .a10(a10), .a9(a9), .a8(a8), .a7(a7), .a6(a6),
    .a5(a5), .a4(a4), .a3(a3), .a2(a2), .a1(a1), .a0(a0), .Cin(Cin), .f15(logicshift_1_f15),
    .f14(logicshift_1_f14), .f13(logicshift_1_f13), .f12(logicshift_1_f12), .f11(logicshift_1_f11),
    .f10(logicshift_1_f10), .f9(logicshift_1_f9), .f8(logicshift_1_f8), .f7(logicshift_1_f7),
    .f6(logicshift_1_f6), .f5(logicshift_1_f5), .f4(logicshift_1_f4), .f3(logicshift_1_f3),
    .f2(logicshift_1_f2), .f1(logicshift_1_f1), .f0(logicshift_1_f0));
  Arit_Left_S arit_left_s_1 (
    .a15(a15), .a14(a14), .a13(a13), .a12(a12), .a11(a11), .a10(a10), .a9(a9), .a8(a8), .a7(a7), .a6(a6),
    .a5(a5), .a4(a4), .a3(a3), .a2(a2), .a1(a1), .a0(a0), .f15(arit_left_s_1_f15), .f14(arit_left_s_1_f14),
    .f13(arit_left_s_1_f13), .f12(arit_left_s_1_f12), .f11(arit_left_s_1_f11), .f10(arit_left_s_1_f10),
    .f9(arit_left_s_1_f9), .f8(arit_left_s_1_f8), .f7(arit_left_s_1_f7), .f6(arit_left_s_1_f6),
    .f5(arit_left_s_1_f5), .f4(arit_left_s_1_f4), .f3(arit_left_s_1_f3), .f2(arit_left_s_1_f2),
    .f1(arit_left_s_1_f1), .f0(arit_left_s_1_f0));
  CircularShift circularshift_1 (
    .a15(a15), .a14(a14), .a13(a13), .a12(a12), .a11(a11), .a10(a10), .a9(a9), .a8(a8), .a7(a7), .a6(a6),
    .a5(a5), .a4(a4), .a3(a3), .a2(a2), .a1(a1), .a0(a0), .Cin(Cin), .f15(circularshift_1_f15),
    .f14(circularshift_1_f14), .f13(circularshift_1_f13), .f12(circularshift_1_f12),
    .f11(circularshift_1_f11), .f10(circularshift_1_f10), .f9(circularshift_1_f9), .f8(circularshift_1_f8),
    .f7(circularshift_1_f7), .f6(circularshift_1_f6), .f5(circularshift_1_f5), .f4(circularshift_1_f4),
    .f3(circularshift_1_f3), .f2(circularshift_1_f2), .f1(circularshift_1_f1), .f0(circularshift_1_f0));
  Arit_Right_S arit_right_s_1 (
    .a15(a15), .a14(a14), .a13(a13), .a12(a12), .a11(a11), .a10(a10), .a9(a9), .a8(a8), .a7(a7), .a6(a6),
    .a5(a5), .a4(a4), .a3(a3), .a2(a2), .a1(a1), .a0(a0), .f15(arit_right_s_1_f15), .f14(arit_right_s_1_f14),
    .f13(arit_right_s_1_f13), .f12(arit_right_s_1_f12), .f11(arit_right_s_1_f11), .f10(arit_right_s_1_f10),
    .f9(arit_right_s_1_f9), .f8(arit_right_s_1_f8), .f7(arit_right_s_1_f7), .f6(arit_right_s_1_f6),
    .f5(arit_right_s_1_f5), .f4(arit_right_s_1_f4), .f3(arit_right_s_1_f3), .f2(arit_right_s_1_f2),
    .f1(arit_right_s_1_f1), .f0(arit_right_s_1_f0));
  WhichShift whichshift_1 (
    .Log(logicshift_1_f15), .ArL(arit_left_s_1_f15), .Cir(circularshift_1_f15), .ArR(arit_right_s_1_f15),
    .s1_s0(s1_s0), .Cin(Cin), .F(f15));
  WhichShift whichshift_2 (
    .Log(logicshift_1_f14), .ArL(arit_left_s_1_f14), .Cir(circularshift_1_f14), .ArR(arit_right_s_1_f14),
    .s1_s0(s1_s0), .Cin(Cin), .F(f14));
  WhichShift whichshift_3 (
    .Log(logicshift_1_f13), .ArL(arit_left_s_1_f13), .Cir(circularshift_1_f13), .ArR(arit_right_s_1_f13),
    .s1_s0(s1_s0), .Cin(Cin), .F(f13));
  WhichShift whichshift_4 (
    .Log(logicshift_1_f12), .ArL(arit_left_s_1_f12), .Cir(circularshift_1_f12), .ArR(arit_right_s_1_f12),
    .s1_s0(s1_s0), .Cin(Cin), .F(f12));
  WhichShift whichshift_5 (
    .Log(logicshift_1_f11), .ArL(arit_left_s_1_f11), .Cir(circularshift_1_f11), .ArR(arit_right_s_1_f11),
    .s1_s0(s1_s0), .Cin(Cin), .F(f11));
  WhichShift whichshift_6 (
    .Log(logicshift_1_f10), .ArL(arit_left_s_1_f10), .Cir(circularshift_1_f10), .ArR(arit_right_s_1_f10),
    .s1_s0(s1_s0), .Cin(Cin), .F(f10));
  WhichShift whichshift_7 (
    .Log(logicshift_1_f9), .ArL(arit_left_s_1_f9), .Cir(circularshift_1_f9), .ArR(arit_right_s_1_f9),
    .s1_s0(s1_s0), .Cin(Cin), .F(f9));
  WhichShift whichshift_8 (
    .Log(logicshift_1_f8), .ArL(arit_left_s_1_f8), .Cir(circularshift_1_f8), .ArR(arit_right_s_1_f8),
    .s1_s0(s1_s0), .Cin(Cin), .F(f8));
  WhichShift whichshift_9 (
    .Log(logicshift_1_f7), .ArL(arit_left_s_1_f7), .Cir(circularshift_1_f7), .ArR(arit_right_s_1_f7),
    .s1_s0(s1_s0), .Cin(Cin), .F(f7));
  WhichShift whichshift_10 (
    .Log(logicshift_1_f6), .ArL(arit_left_s_1_f6), .Cir(circularshift_1_f6), .ArR(arit_right_s_1_f6),
    .s1_s0(s1_s0), .Cin(Cin), .F(f6));
  WhichShift whichshift_11 (
    .Log(logicshift_1_f5), .ArL(arit_left_s_1_f5), .Cir(circularshift_1_f5), .ArR(arit_right_s_1_f5),
    .s1_s0(s1_s0), .Cin(Cin), .F(f5));
  WhichShift whichshift_12 (
    .Log(logicshift_1_f4), .ArL(arit_left_s_1_f4), .Cir(circularshift_1_f4), .ArR(arit_right_s_1_f4),
    .s1_s0(s1_s0), .Cin(Cin), .F(f4));
  WhichShift whichshift_13 (
    .Log(logicshift_1_f3), .ArL(arit_left_s_1_f3), .Cir(circularshift_1_f3), .ArR(arit_right_s_1_f3),
    .s1_s0(s1_s0), .Cin(Cin), .F(f3));
  WhichShift whichshift_14 (
    .Log(logicshift_1_f2), .ArL(arit_left_s_1_f2), .Cir(circularshift_1_f2), .ArR(arit_right_s_1_f2),
    .s1_s0(s1_s0), .Cin(Cin), .F(f2));
  WhichShift whichshift_15 (
    .Log(logicshift_1_f1), .ArL(arit_left_s_1_f1), .Cir(circularshift_1_f1), .ArR(arit_right_s_1_f1),
    .s1_s0(s1_s0), .Cin(Cin), .F(f1));
  WhichShift whichshift_16 (
    .Log(logicshift_1_f0), .ArL(arit_left_s_1_f0), .Cir(circularshift_1_f0), .ArR(arit_right_s_1_f0),
    .s1_s0(s1_s0), .Cin(Cin), .F(out_34));
endmodule

module WhichShift (
  input  Log,
  input  ArL,
  input  Cir,
  input  ArR,
  input  [1:0] s1_s0,
  input  Cin,
  output F
);

  wire multiplexer_1_out, multiplexer_2_out;

  Multiplexer #(.select(2), .enable("false")) multiplexer_1 (
    .in0(Log), .in1(Cir), .in2(ArL), .out(multiplexer_1_out), .sel(s1_s0));  // open: in3
  Multiplexer #(.select(2), .enable("false")) multiplexer_2 (
    .in0(ArR), .in1(Log), .in2(Cir), .out(multiplexer_2_out), .sel(s1_s0));  // open: in3
  Multiplexer #(.enable("false")) multiplexer_3 (.in0(multiplexer_1_out), .in1(multiplexer_2_out), .out(F), .sel(Cin));
endmodule

module Arit_Left_S (
  input  a15,
  input  a14,
  input  a13,
  input  a12,
  input  a11,
  input  a10,
  input  a9,
  input  a8,
  input  a7,
  input  a6,
  input  a5,
  input  a4,
  input  a3,
  input  a2,
  input  a1,
  input  a0,
  output f15,
  output f14,
  output f13,
  output f12,
  output f11,
  output f10,
  output f9,
  output f8,
  output f7,
  output f6,
  output f5,
  output f4,
  output f3,
  output f2,
  output f1,
  output f0
);

  not not_1 (f0, 1'b1);

  assign f1 = a0;
  assign f2 = a1;
  assign f3 = a2;
  assign f4 = a3;
  assign f5 = a4;
  assign f6 = a5;
  assign f7 = a6;
  assign f8 = a7;
  assign f9 = a8;
  assign f10 = a9;
  assign f11 = a10;
  assign f12 = a11;
  assign f13 = a12;
  assign f14 = a13;
  assign f15 = a14;
endmodule

module ALSU_16b (
  input  Cin,
  input  a0,
  input  b0,
  input  a1,
  input  b1,
  input  a2,
  input  b2,
  input  a3,
  input  b3,
  input  a4,
  input  b4,
  input  a5,
  input  b5,
  input  a6,
  input  b6,
  input  a7,
  input  b7,
  input  a8,
  input  b8,
  input  a9,
  input  b9,
  input  a10,
  input  b10,
  input  a11,
  input  b11,
  input  a12,
  input  b12,
  input  a13,
  input  b13,
  input  a14,
  input  b14,
  input  a15,
  input  b15,
  input  [1:0] s1_s0,
  input  [1:0] s3_s2,
  output N_Flag,
  output _0_Flag,
  output C_Flag,
  output Z_flag,
  output f0,
  output f1,
  output f2,
  output f3,
  output f4,
  output f5,
  output f6,
  output f7,
  output f8,
  output f9,
  output f10,
  output f11,
  output f12,
  output f13,
  output f14,
  output f15,
  output Cout
);

  wire alu_16b_1_cout, alu_16b_1_f0, alu_16b_1_f1, alu_16b_1_f2, alu_16b_1_f3, alu_16b_1_f4, alu_16b_1_f5,
       alu_16b_1_f6, alu_16b_1_f7, alu_16b_1_f8, alu_16b_1_f9, alu_16b_1_f10, alu_16b_1_f11, alu_16b_1_f12,
       alu_16b_1_f13, alu_16b_1_f14, alu_16b_1_f15, shiftoperation_16b_1_f1, shiftoperation_16b_1_f2,
       shiftoperation_16b_1_f3, shiftoperation_16b_1_f4, shiftoperation_16b_1_f5, shiftoperation_16b_1_f6,
       shiftoperation_16b_1_f7, shiftoperation_16b_1_f8, shiftoperation_16b_1_f9, shiftoperation_16b_1_f10,
       shiftoperation_16b_1_f11, shiftoperation_16b_1_f12, shiftoperation_16b_1_f13,
       shiftoperation_16b_1_f14, shiftoperation_16b_1_f15, shiftoperation_16b_1_out_34;

  Alu_16b alu_16b_1 (
    .Cin(Cin), .a0(a0), .b0(b0), .a1(a1), .b1(b1), .a2(a2), .b2(b2), .a3(a3), .b3(b3), .a4(a4), .b4(b4),
    .a5(a5), .b5(b5), .a6(a6), .b6(b6), .a7(a7), .b7(b7), .a8(a8), .b8(b8), .a9(a9), .b9(b9), .a10(a10),
    .b10(b10), .a11(a11), .b11(b11), .a12(a12), .b12(b12), .a13(a13), .b13(b13), .a14(a14), .b14(b14),
    .a15(a15), .b15(b15), .s1_s0(s1_s0), .s3_s2(s3_s2), .O_Flag(_0_Flag), .C_flag(C_Flag), .f0(alu_16b_1_f0),
    .f1(alu_16b_1_f1), .f2(alu_16b_1_f2), .f3(alu_16b_1_f3), .f4(alu_16b_1_f4), .f5(alu_16b_1_f5),
    .f6(alu_16b_1_f6), .f7(alu_16b_1_f7), .f8(alu_16b_1_f8), .f9(alu_16b_1_f9), .f10(alu_16b_1_f10),
    .f11(alu_16b_1_f11), .f12(alu_16b_1_f12), .f13(alu_16b_1_f13), .f14(alu_16b_1_f14), .f15(alu_16b_1_f15),
    .Cout(alu_16b_1_cout));  // open: Z_flag, N_Flag
  ShiftOperation_16b shiftoperation_16b_1 (
    .a15(a15), .a14(a14), .a13(a13), .a12(a12), .a11(a11), .a10(a10), .a9(a9), .a8(a8), .a7(a7), .a6(a6),
    .a5(a5), .a4(a4), .a3(a3), .a2(a2), .a1(a1), .a0(a0), .s1_s0(s1_s0), .Cin(Cin),
    .f15(shiftoperation_16b_1_f15), .f14(shiftoperation_16b_1_f14), .f13(shiftoperation_16b_1_f13),
    .f12(shiftoperation_16b_1_f12), .f11(shiftoperation_16b_1_f11), .f10(shiftoperation_16b_1_f10),
    .f9(shiftoperation_16b_1_f9), .f8(shiftoperation_16b_1_f8), .f7(shiftoperation_16b_1_f7),
    .f6(shiftoperation_16b_1_f6), .f5(shiftoperation_16b_1_f5), .f4(shiftoperation_16b_1_f4),
    .f3(shiftoperation_16b_1_f3), .f2(shiftoperation_16b_1_f2), .f1(shiftoperation_16b_1_f1),
    .out_34(shiftoperation_16b_1_out_34));
  Multiplexer #(.select(2), .enable("false")) multiplexer_1 (
    .in0(shiftoperation_16b_1_out_34), .in1(alu_16b_1_f0), .in2(alu_16b_1_f0), .out(f0), .sel(s3_s2));  // open: in3
  Multiplexer #(.select(2), .enable("false")) multiplexer_2 (
    .in0(shiftoperation_16b_1_f1), .in1(alu_16b_1_f1), .in2(alu_16b_1_f1), .out(f1), .sel(s3_s2));  // open: in3
  Multiplexer #(.select(2), .enable("false")) multiplexer_3 (
    .in0(shiftoperation_16b_1_f2), .in1(alu_16b_1_f2), .in2(alu_16b_1_f2), .out(f2), .sel(s3_s2));  // open: in3
  Multiplexer #(.select(2), .enable("false")) multiplexer_4 (
    .in0(shiftoperation_16b_1_f3), .in1(alu_16b_1_f3), .in2(alu_16b_1_f3), .out(f3), .sel(s3_s2));  // open: in3
  Multiplexer #(.select(2), .enable("false")) multiplexer_5 (
    .in0(shiftoperation_16b_1_f4), .in1(alu_16b_1_f4), .in2(alu_16b_1_f4), .out(f4), .sel(s3_s2));  // open: in3
  Multiplexer #(.select(2), .enable("false")) multiplexer_6 (
    .in0(shiftoperation_16b_1_f5), .in1(alu_16b_1_f5), .in2(alu_16b_1_f5), .out(f5), .sel(s3_s2));  // open: in3
  Multiplexer #(.select(2), .enable("false")) multiplexer_7 (
    .in0(shiftoperation_16b_1_f6), .in1(alu_16b_1_f6), .in2(alu_16b_1_f6), .out(f6), .sel(s3_s2));  // open: in3
  Multiplexer #(.select(2), .enable("false")) multiplexer_8 (
    .in0(shiftoperation_16b_1_f7), .in1(alu_16b_1_f7), .in2(alu_16b_1_f7), .out(f7), .sel(s3_s2));  // open: in3
  Multiplexer #(.select(2), .enable("false")) multiplexer_9 (
    .in0(shiftoperation_16b_1_f8), .in1(alu_16b_1_f8), .in2(alu_16b_1_f8), .out(f8), .sel(s3_s2));  // open: in3
  Multiplexer #(.select(2), .enable("false")) multiplexer_10 (
    .in0(shiftoperation_16b_1_f9), .in1(alu_16b_1_f9), .in2(alu_16b_1_f9), .out(f9), .sel(s3_s2));  // open: in3
  Multiplexer #(.select(2), .enable("false")) multiplexer_11 (
    .in0(shiftoperation_16b_1_f10), .in1(alu_16b_1_f10), .in2(alu_16b_1_f10), .out(f10), .sel(s3_s2));  // open: in3
  Multiplexer #(.select(2), .enable("false")) multiplexer_12 (
    .in0(shiftoperation_16b_1_f11), .in1(alu_16b_1_f11), .in2(alu_16b_1_f11), .out(f11), .sel(s3_s2));  // open: in3
  Multiplexer #(.select(2), .enable("false")) multiplexer_13 (
    .in0(shiftoperation_16b_1_f12), .in1(alu_16b_1_f12), .in2(alu_16b_1_f12), .out(f12), .sel(s3_s2));  // open: in3
  Multiplexer #(.select(2), .enable("false")) multiplexer_14 (
    .in0(shiftoperation_16b_1_f13), .in1(alu_16b_1_f13), .in2(alu_16b_1_f13), .out(f13), .sel(s3_s2));  // open: in3
  Multiplexer #(.select(2), .enable("false")) multiplexer_15 (
    .in0(shiftoperation_16b_1_f14), .in1(alu_16b_1_f14), .in2(alu_16b_1_f14), .out(f14), .sel(s3_s2));  // open: in3
  Multiplexer #(.select(2), .enable("false")) multiplexer_16 (
    .in0(shiftoperation_16b_1_f15), .in1(alu_16b_1_f15), .in2(alu_16b_1_f15), .out(f15), .sel(s3_s2));  // open: in3
  nor nor_1 (Z_flag, f0, f1, f2, f3, f4, f5, f6, f7, f8, f9, f10, f11, f12, f13, f14, f15);
  Multiplexer #(.select(2), .enable("false")) multiplexer_17 (
    .in2(alu_16b_1_cout), .out(Cout), .sel(s3_s2));  // open: in0, in1, in3

  assign N_Flag = f15;
endmodule

module Register_8bit (
  input  R_in,
  input  R,
  input  R_2,
  input  I,
  input  Z,
  input  N,
  input  O,
  input  C,
  output R_out,
  output R_3,
  output R_4,
  output I_2,
  output Z_2,
  output N_2,
  output O_2,
  output C_2
);

  wire clock_1_out;

  Clock clock_1 (.out(clock_1_out));
  D_Flip_Flop d_ff_1 (.clk(clock_1_out), .D(R_in), .Q(R_out));  // open: Qn, preset, en, reset
  D_Flip_Flop d_ff_2 (.clk(clock_1_out), .D(R), .Q(R_3));  // open: Qn, preset, en, reset
  D_Flip_Flop d_ff_3 (.clk(clock_1_out), .D(R_2), .Q(R_4));  // open: Qn, preset, en, reset
  D_Flip_Flop d_ff_4 (.clk(clock_1_out), .D(I), .Q(I_2));  // open: Qn, preset, en, reset
  D_Flip_Flop d_ff_5 (.clk(clock_1_out), .D(Z), .Q(Z_2));  // open: Qn, preset, en, reset
  D_Flip_Flop d_ff_6 (.clk(clock_1_out), .D(N), .Q(N_2));  // open: Qn, preset, en, reset
  D_Flip_Flop d_ff_7 (.clk(clock_1_out), .D(O), .Q(O_2));  // open: Qn, preset, en, reset
  D_Flip_Flop d_ff_8 (.clk(clock_1_out), .D(C), .Q(C_2));  // open: Qn, preset, en, reset
endmodule

module ALU_Complete (
  input  Cin,
  input  a0,
  input  b0,
  input  a1,
  input  b1,
  input  a2,
  input  b2,
  input  a3,
  input  b3,
  input  a4,
  input  b4,
  input  a5,
  input  b5,
  input  a6,
  input  b6,
  input  a7,
  input  b7,
  input  a8,
  input  b8,
  input  a9,
  input  b9,
  input  a10,
  input  b10,
  input  a11,
  input  b11,
  input  a12,
  input  b12,
  input  a13,
  input  b13,
  input  a14,
  input  b14,
  input  a15,
  input  b15,
  input  [1:0] s1_s0,
  input  [1:0] s3_s2,
  input  R,
  input  R_2,
  input  R_3,
  input  I,
  input  Z,
  input  N,
  input  O,
  input  C,
  output Z_Flag,
  output N_Flag,
  output O_Flag,
  output C_Flag,
  output f0,
  output f1,
  output f2,
  output f3,
  output f4,
  output f5,
  output f6,
  output f7,
  output f8,
  output f9,
  output f10,
  output f11,
  output f12,
  output f13,
  output f14,
  output f15,
  output Cout,
  output R_4,
  output R_5,
  output R_6,
  output I_2
);

  ALSU_16b alsu_16b_1 (
    .Cin(Cin), .a0(a0), .b0(b0), .a1(a1), .b1(b1), .a2(a2), .b2(b2), .a3(a3), .b3(b3), .a4(a4), .b4(b4),
    .a5(a5), .b5(b5), .a6(a6), .b6(b6), .a7(a7), .b7(b7), .a8(a8), .b8(b8), .a9(a9), .b9(b9), .a10(a10),
    .b10(b10), .a11(a11), .b11(b11), .a12(a12), .b12(b12), .a13(a13), .b13(b13), .a14(a14), .b14(b14),
    .a15(a15), .b15(b15), .s1_s0(s1_s0), .s3_s2(s3_s2), .Z_flag(Z_Flag), .N_Flag(N_Flag), ._0_Flag(O_Flag),
    .C_Flag(C_Flag), .f0(f0), .f1(f1), .f2(f2), .f3(f3), .f4(f4), .f5(f5), .f6(f6), .f7(f7), .f8(f8),
    .f9(f9), .f10(f10), .f11(f11), .f12(f12), .f13(f13), .f14(f14), .f15(f15), .Cout(Cout));

  assign I_2 = I;
  assign R_4 = R;
  assign R_5 = R_2;
  assign R_6 = R_3;
endmodule
