// Logisim project 16bitALU.circ as structural Verilog: 5 circuits, main circuit main
module main (
  input  Cin,
  input  [3:0] S,
  input  [15:0] A,
  input  [15:0] B,
  output [15:0] Output,
  output Cout
);

  _16bit u_16bit_1 (.S(S), .A(A), .Cin(Cin), .Output(Output), .B(B), .Cout(Cout));
  Hex_Digit_Display hex_digit_display_1 (.value(Output[11:8]));  // open: dp
  Hex_Digit_Display hex_digit_display_2 (.value(Output[15:12]));  // open: dp
  Hex_Digit_Display hex_digit_display_3 (.value(Output[3:0]));  // open: dp
  Hex_Digit_Display hex_digit_display_4 (.value(Output[7:4]));  // open: dp
endmodule

module _16bit (
  input  [3:0] S,
  input  [15:0] A,
  input  Cin,
  input  [15:0] B,
  output [15:0] Output,
  output Cout
);

  wire and_1_out, and_2_out, and_3_out, and_4_out, and_5_out, n1bit_1_cout, n1bit_2_cout, n1bit_3_cout,
       n1bit_4_cout, n1bit_5_cout, n1bit_6_cout, n1bit_7_cout, n1bit_8_cout, n1bit_9_cout, n1bit_10_cout,
       n1bit_11_cout, n1bit_12_cout, n1bit_13_cout, n1bit_14_cout, n1bit_15_cout, not_1_out, not_2_out,
       not_3_out, not_4_out, or_1_out, or_2_out, or_3_out;

  not not_1 (not_1_out, S[2]);
  not not_2 (not_2_out, or_1_out);
  or or_1 (or_1_out, S[1], S[0]);
  not not_3 (not_3_out, S[2]);
  or or_2 (or_2_out, S[1], S[0]);
  not not_4 (not_4_out, or_2_out);
  and and_1 (and_1_out, A[15], not_2_out, not_3_out);
  and and_2 (and_2_out, A[14], not_1_out);
  and and_3 (and_3_out, A[0], not_4_out);
  and and_4 (and_4_out, A[15], S[1]);
  and and_5 (and_5_out, S[2], A[1]);
  _1bit u_1bit_1 (
    .A_i(A[0]), .B_i(B[0]), .S0(S[0]), .S1(S[1]), .S2(S[2]), .S3(S[3]), .A_i_1(and_1_out),
    .A_i_1_2(and_5_out), .Cin(Cin), .Cout(n1bit_1_cout), .Output(Output[0]));
  _1bit u_1bit_2 (
    .A_i(A[1]), .B_i(B[1]), .S0(S[0]), .S1(S[1]), .S2(S[2]), .S3(S[3]), .A_i_1(A[0]), .A_i_1_2(A[2]),
    .Cin(n1bit_1_cout), .Cout(n1bit_2_cout), .Output(Output[1]));
  _1bit u_1bit_3 (
    .A_i(A[2]), .B_i(B[2]), .S0(S[0]), .S1(S[1]), .S2(S[2]), .S3(S[3]), .A_i_1(A[1]), .A_i_1_2(A[3]),
    .Cin(n1bit_2_cout), .Cout(n1bit_3_cout), .Output(Output[2]));
  _1bit u_1bit_4 (
    .A_i(A[3]), .B_i(B[3]), .S0(S[0]), .S1(S[1]), .S2(S[2]), .S3(S[3]), .A_i_1(A[2]), .A_i_1_2(A[4]),
    .Cin(n1bit_3_cout), .Cout(n1bit_4_cout), .Output(Output[3]));
  _1bit u_1bit_5 (
    .A_i(A[4]), .B_i(B[4]), .S0(S[0]), .S1(S[1]), .S2(S[2]), .S3(S[3]), .A_i_1(A[3]), .A_i_1_2(A[5]),
    .Cin(n1bit_4_cout), .Cout(n1bit_5_cout), .Output(Output[4]));
  _1bit u_1bit_6 (
    .A_i(A[5]), .B_i(B[5]), .S0(S[0]), .S1(S[1]), .S2(S[2]), .S3(S[3]), .A_i_1(A[4]), .A_i_1_2(A[6]),
    .Cin(n1bit_5_cout), .Cout(n1bit_6_cout), .Output(Output[5]));
  _1bit u_1bit_7 (
    .A_i(A[6]), .B_i(B[6]), .S0(S[0]), .S1(S[1]), .S2(S[2]), .S3(S[3]), .A_i_1(A[5]), .A_i_1_2(A[7]),
    .Cin(n1bit_6_cout), .Cout(n1bit_7_cout), .Output(Output[6]));
  _1bit u_1bit_8 (
    .A_i(A[7]), .B_i(B[7]), .S0(S[0]), .S1(S[1]), .S2(S[2]), .S3(S[3]), .A_i_1(A[6]), .A_i_1_2(A[8]),
    .Cin(n1bit_7_cout), .Cout(n1bit_8_cout), .Output(Output[7]));
  _1bit u_1bit_9 (
    .A_i(A[8]), .B_i(B[8]), .S0(S[0]), .S1(S[1]), .S2(S[2]), .S3(S[3]), .A_i_1(A[7]), .A_i_1_2(A[9]),
    .Cin(n1bit_8_cout), .Cout(n1bit_9_cout), .Output(Output[8]));
  _1bit u_1bit_10 (
    .A_i(A[9]), .B_i(B[9]), .S0(S[0]), .S1(S[1]), .S2(S[2]), .S3(S[3]), .A_i_1(A[8]), .A_i_1_2(A[10]),
    .Cin(n1bit_9_cout), .Cout(n1bit_10_cout), .Output(Output[9]));
  _1bit u_1bit_11 (
    .A_i(A[10]), .B_i(B[10]), .S0(S[0]), .S1(S[1]), .S2(S[2]), .S3(S[3]), .A_i_1(A[9]), .A_i_1_2(A[11]),
    .Cin(n1bit_10_cout), .Cout(n1bit_11_cout), .Output(Output[10]));
  _1bit u_1bit_12 (
    .A_i(A[11]), .B_i(B[11]), .S0(S[0]), .S1(S[1]), .S2(S[2]), .S3(S[3]), .A_i_1(A[10]), .A_i_1_2(A[12]),
    .Cin(n1bit_11_cout), .Cout(n1bit_12_cout), .Output(Output[11]));
  _1bit u_1bit_13 (
    .A_i(A[12]), .B_i(B[12]), .S0(S[0]), .S1(S[1]), .S2(S[2]), .S3(S[3]), .A_i_1(A[11]), .A_i_1_2(A[13]),
    .Cin(n1bit_12_cout), .Cout(n1bit_13_cout), .Output(Output[12]));
  _1bit u_1bit_14 (
    .A_i(A[13]), .B_i(B[13]), .S0(S[0]), .S1(S[1]), .S2(S[2]), .S3(S[3]), .A_i_1(A[12]), .A_i_1_2(A[14]),
    .Cin(n1bit_13_cout), .Cout(n1bit_14_cout), .Output(Output[13]));
  _1bit u_1bit_15 (
    .A_i(A[14]), .B_i(B[14]), .S0(S[0]), .S1(S[1]), .S2(S[2]), .S3(S[3]), .A_i_1(A[13]), .A_i_1_2(A[15]),
    .Cin(n1bit_14_cout), .Cout(n1bit_15_cout), .Output(Output[14]));
  _1bit u_1bit_16 (
    .A_i(A[15]), .B_i(B[15]), .S0(S[0]), .S1(S[1]), .S2(S[2]), .S3(S[3]), .A_i_1(and_2_out),
    .A_i_1_2(or_3_out), .Cin(n1bit_15_cout), .Cout(Cout), .Output(Output[15]));
  or or_3 (or_3_out, and_3_out, and_4_out);
endmodule

module _1bit (
  input  Cin,
  input  A_i,
  input  B_i,
  input  S0,
  input  S1,
  input  S2,
  input  S3,
  input  A_i_1,
  input  A_i_1_2,
  output Output,
  output Cout
);

  wire arithmetic_1_output, logic_1_output;

  arithmetic arithmetic_1 (.Cin(Cin), .A(A_i), .B(B_i), .S0(S0), .S1(S1), .Cout(Cout), .Output(arithmetic_1_output));
  \logic  logic_1 (.A(A_i), .B(B_i), .S0(S0), .S1(S1), .Output(logic_1_output));
  Multiplexer #(.select(2), .enable("false")) multiplexer_1 (
    .in0(arithmetic_1_output), .in1(logic_1_output), .in2(A_i_1), .in3(A_i_1_2), .out(Output), .sel({S3, S2}));
endmodule

module arithmetic (
  input  Cin,
  input  A,
  input  B,
  input  S0,
  input  S1,
  output Output,
  output Cout
);

  wire multiplexer_1_out, not_1_out;

  not not_1 (not_1_out, B);
  Multiplexer #(.select(2), .enable("false")) multiplexer_1 (
    .in0(1'b0), .in1(B), .in2(not_1_out), .in3(1'b1), .out(multiplexer_1_out), .sel({S1, S0}));
  Adder #(.width(1)) adder_1 (.a(A), .b(multiplexer_1_out), .out(Output), .cin(Cin), .cout(Cout));
endmodule

module \logic  (
  input  A,
  input  B,
  input  S0,
  input  S1,
  output Output
);

  wire and_1_out, not_1_out, or_1_out, xor_1_out;

  and and_1 (and_1_out, A, B);
  or or_1 (or_1_out, A, B);
  xor xor_1 (xor_1_out, A, B);
  not not_1 (not_1_out, A);
  Multiplexer #(.select(2), .enable("false")) multiplexer_1 (
    .in0(and_1_out), .in1(or_1_out), .in2(xor_1_out), .in3(not_1_out), .out(Output), .sel({S1, S0}));
endmodule
