// Logisim project simplecomputer.circ as structural Verilog: 1 circuit, main circuit main
// LD
module main (
  input  [1:0] c1c0,
  input  [1:0] d1d0,
  input  [1:0] b1b0,
  input  Write,
  input  Read,
  input  CLR,
  input  LD,
  input  INC,
  input  CLR_2,
  input  LD_2,
  input  INC_2,
  input  CLR_3,
  input  LD_3,
  input  INC_3,
  input  CLR_4,
  input  LD_4,
  input  INC_4,
  input  [7:0] in_18,
  input  in_V_ac,
  input  LD_5,
  input  [1:0] in_21,
  input  [1:0] in_22,
  input  CLR_5,
  input  LD_6,
  input  INC_5,
  input  CLR_6,
  input  LD_7,
  input  INC_6,
  input  CLR_7,
  input  LD_8,
  input  INC_7,
  input  LD_9,
  output [15:0] out_33,
  output [15:0] out_34,
  output [7:0] out_35
);

  wire clock_1_out, decoder_1_out0, decoder_1_out1, decoder_1_out2, decoder_2_out0, decoder_2_out1,
       decoder_2_out2, decoder_2_out3;
  wire [7:0] bit_extender_5_out, INPUT_output, register_1_q, test_1_ccr_out;
  wire [11:0] AR_output, bit_extender_1_out, bit_extender_2_out, bit_extender_3_out, bit_extender_4_out,
       PC_output, SP_output;
  wire [15:0] AC_output, bit_extender_6_out, bit_extender_7_out, bit_extender_8_out, bit_extender_9_out,
       controlled_buffer_1_out, DR_output, IR_output, multiplexer_1_out, multiplexer_2_out, ram_1_data,
       TR_output;

  Multiplexer #(.select(2), .width(16)) multiplexer_1 (
    .in0(ram_1_data), .in1(controlled_buffer_1_out), .in2(out_33), .out(multiplexer_1_out), .sel(b1b0));  // open: in3, en
  Clock clock_1 (.out(clock_1_out));
  Bit_Extender #(.in_width(16), .out_width(12)) bit_extender_1 (.in(multiplexer_1_out), .out(bit_extender_1_out));
  Bit_Extender #(.in_width(16), .out_width(12)) bit_extender_2 (.in(multiplexer_1_out), .out(bit_extender_2_out));
  Bit_Extender #(.in_width(16), .out_width(12)) bit_extender_3 (.in(multiplexer_1_out), .out(bit_extender_3_out));
  Bit_Extender #(.in_width(16), .out_width(12)) bit_extender_4 (.in(multiplexer_1_out), .out(bit_extender_4_out));
  Bit_Extender #(.in_width(16), .out_width(8)) bit_extender_5 (.in(multiplexer_1_out), .out(bit_extender_5_out));
  _12bitReg_main PC (.INPUT(bit_extender_2_out), .CLK(clock_1_out), .INC(INC), .LD(LD), .CLR(CLR), .OUTPUT(PC_output));
  _12bitReg_main AR (
    .INPUT(bit_extender_3_out), .CLK(clock_1_out), .INC(INC_2), .LD(LD_2), .CLR(CLR_2), .OUTPUT(AR_output));
  _12bitReg_main SP (
    .INPUT(bit_extender_4_out), .CLK(clock_1_out), .INC(INC_3), .LD(LD_3), .CLR(CLR_3), .OUTPUT(SP_output));
  _16bitReg_main DR (
    .INPUT(multiplexer_1_out), .CLK(clock_1_out), .INC(INC_4), .LD(LD_4), .CLR(CLR_4), .OUTPUT(DR_output));
  assign bit_extender_6_out = {{8{1'b0}}, INPUT_output};  // Bit_Extender bit_extender_6
  _8bitReg_main INPUT (.INPUT(in_18), .CLK(clock_1_out), .LD(LD_5), .OUTPUT(INPUT_output));  // open: INC, CLR
  _16bitReg_main AC (.INPUT(out_34), .CLK(clock_1_out), .INC(INC_5), .LD(LD_6), .CLR(CLR_5), .OUTPUT(AC_output));
  _16bitReg_main IR (
    .INPUT(multiplexer_1_out), .CLK(clock_1_out), .INC(INC_6), .LD(LD_7), .CLR(CLR_6), .OUTPUT(IR_output));
  _16bitReg_main TR (
    .INPUT(multiplexer_1_out), .CLK(clock_1_out), .INC(INC_7), .LD(LD_8), .CLR(CLR_7), .OUTPUT(TR_output));
  RAM #(.addrWidth(12), .dataWidth(16), .bus("separate")) ram_1 (
    .addr(bit_extender_1_out), .data(ram_1_data), .str(Write), .clk(clock_1_out), .ld(Read));  // open: din, sel, clr
  assign bit_extender_7_out = {{4{1'b0}}, PC_output};  // Bit_Extender bit_extender_7
  assign bit_extender_8_out = {{4{1'b0}}, AR_output};  // Bit_Extender bit_extender_8
  assign bit_extender_9_out = {{4{1'b0}}, SP_output};  // Bit_Extender bit_extender_9
  Multiplexer #(.width(16)) multiplexer_2 (
    .in0(bit_extender_6_out), .in1(AC_output), .out(multiplexer_2_out), .sel(in_V_ac));  // open: en
  _8bitReg_main OUTPUT (.INPUT(bit_extender_5_out), .CLK(clock_1_out), .LD(LD_9), .OUTPUT(out_35));  // open: INC, CLR
  Decoder #(.select(2)) decoder_1 (
    .out0(decoder_1_out0), .out1(decoder_1_out1), .out2(decoder_1_out2), .sel(c1c0));  // open: out3, en
  assign controlled_buffer_1_out = decoder_1_out0 ? bit_extender_7_out : 16'bz;  // Controlled_Buffer controlled_buffer_1
  assign controlled_buffer_1_out = decoder_1_out1 ? bit_extender_8_out : 16'bz;  // Controlled_Buffer controlled_buffer_2
  assign controlled_buffer_1_out = decoder_1_out2 ? bit_extender_9_out : 16'bz;  // Controlled_Buffer controlled_buffer_3
  test test_1 (
    .CCR_IN(register_1_q), .in_2(DR_output), .in_3(multiplexer_2_out), .s1_s0(in_21), .s3_s2(in_22),
    .out_6(out_34), .CCR_OUT(test_1_ccr_out));
  assign out_33 = decoder_2_out1 ? AC_output : 16'bz;  // Controlled_Buffer controlled_buffer_4
  assign out_33 = decoder_2_out2 ? IR_output : 16'bz;  // Controlled_Buffer controlled_buffer_5
  assign out_33 = decoder_2_out3 ? TR_output : 16'bz;  // Controlled_Buffer controlled_buffer_6
  assign out_33 = decoder_2_out0 ? DR_output : 16'bz;  // Controlled_Buffer controlled_buffer_7
  Decoder #(.select(2)) decoder_2 (
    .out0(decoder_2_out0), .out1(decoder_2_out1), .out2(decoder_2_out2), .out3(decoder_2_out3), .sel(d1d0));  // open: en
  Register register_1 (.D(test_1_ccr_out), .Q(register_1_q), .clk(clock_1_out));  // open: en, clr
  Hex_Digit_Display hex_digit_display_1 (.value(out_34[15:12]));  // open: dp
  Hex_Digit_Display hex_digit_display_2 (.value(out_34[11:8]));  // open: dp
  Hex_Digit_Display hex_digit_display_3 (.value(out_34[7:4]));  // open: dp
  Hex_Digit_Display hex_digit_display_4 (.value(out_34[3:0]));  // open: dp
endmodule
